// Digital circuit GAL16V8.dig as structural Verilog
module GAL16V8 (
  input  I_0_Clk,
  input  I_1,
  input  I_2,
  input  I_3,
  input  I_4,
  input  I_5,
  input  I_6,
  input  I_7,
  input  I_8,
  input  GND,
  input  I_17_nOE,
  input  I_9,
  input  I_10,
  input  I_11,
  input  I_12,
  input  I_13,
  input  I_14,
  input  I_15,
  input  I_16,
  output Q_7,
  output Q_6,
  output Q_5,
  output Q_4,
  output Q_3,
  output Q_2,
  output Q_1,
  output Q_0,
  output VCC
);

  wire comparator_1_lt, fuse_matrix_1_p5, fuse_matrix_2_p5, fuse_matrix_3_p5, fuse_matrix_4_p5,
       fuse_matrix_5_p5, fuse_matrix_6_p5, fuse_matrix_7_p5, fuse_matrix_8_p5, I_9_t, I_10_t, I_11_t, I_12_t,
       I_13_t, I_14_t, I_15_t, I_16_t, M_en, nOE, olmc_1_p7, olmc_1_p8, olmc_2_p7, olmc_2_p8, olmc_3_p7,
       olmc_3_p8, olmc_4_p7, olmc_4_p8, olmc_5_p7, olmc_5_p8, olmc_6_p7, olmc_6_p8, olmc_7_p7, olmc_7_p8,
       olmc_8_p7, olmc_8_p8, Q_0_t, Q_1_t, Q_2_t, Q_3_t, Q_4_t, Q_5_t, Q_6_t, Q_7_t;
  wire [0:0] M_7;
  wire [1:0] M_5, M_6;
  wire [2:0] M_2, M_3, M_4;
  wire [3:0] M_0, M_1;
  wire [6:0] counter_1_out;
  wire [7:0] decoder_1_out_7, decoder_2_out_7, driver_1_out, driver_2_out, driver_3_out, driver_4_out,
       driver_5_out, driver_6_out, driver_7_out, driver_8_out, x_en, y_en;
  wire [13:0] register_1_q;
  wire [30:0] SQ;
  wire [31:0] F;

  Comparator #(.Bits(7)) comparator_1 (.a(counter_1_out), .b(7'b1000001), .eq(VCC), .lt(comparator_1_lt));  // open: gt
  Counter #(.Bits(7)) counter_1 (.en(comparator_1_lt), .C(GND), .clr(1'b0), .out(counter_1_out));  // open: ovf
  ROM #(.AddrBits(7), .Bits(32)) Fuses (.A(counter_1_out), .sel(1'b1), .D(F));
  Decoder #(.Selector_Bits(3)) decoder_1 (
    .sel(counter_1_out[2:0]), .out_0(decoder_1_out_7[0]), .out_1(decoder_1_out_7[1]),
    .out_2(decoder_1_out_7[2]), .out_3(decoder_1_out_7[3]), .out_4(decoder_1_out_7[4]),
    .out_5(decoder_1_out_7[5]), .out_6(decoder_1_out_7[6]), .out_7(decoder_1_out_7[7]));
  Decoder #(.Selector_Bits(3)) decoder_2 (
    .sel(counter_1_out[5:3]), .out_0(decoder_2_out_7[0]), .out_1(decoder_2_out_7[1]),
    .out_2(decoder_2_out_7[2]), .out_3(decoder_2_out_7[3]), .out_4(decoder_2_out_7[4]),
    .out_5(decoder_2_out_7[5]), .out_6(decoder_2_out_7[6]), .out_7(decoder_2_out_7[7]));
  assign x_en = ~counter_1_out[6] ? decoder_1_out_7 : 8'bz;  // DriverInvSel driverinvsel_1
  and and_1 (M_en, decoder_1_out_7[0], decoder_2_out_7[0], counter_1_out[6]);
  assign y_en = ~counter_1_out[6] ? decoder_2_out_7 : 8'bz;  // DriverInvSel driverinvsel_2
  PullDown #(.Bits(8)) pulldown_1 (.out(x_en));
  PullDown #(.Bits(8)) pulldown_2 (.out(y_en));
  Register #(.Bits(32)) register_1 (
    .D(F), .C(GND), .en(M_en),
    .Q({M_0[0], M_1[0], M_2[0], M_3[0], M_4[0], M_5[0], M_6[0], M_7[0], M_0[2], M_1[2], M_2[2], M_3[2], M_4[2:1], M_5[1], M_6[1], M_0[1], M_1[3], register_1_q}));
  assign driver_1_out = y_en[0] ? x_en : 8'bz;  // Driver driver_1
  assign driver_2_out = y_en[1] ? x_en : 8'bz;  // Driver driver_2
  assign driver_3_out = y_en[2] ? x_en : 8'bz;  // Driver driver_3
  assign driver_4_out = y_en[3] ? x_en : 8'bz;  // Driver driver_4
  assign driver_5_out = y_en[4] ? x_en : 8'bz;  // Driver driver_5
  assign driver_6_out = y_en[5] ? x_en : 8'bz;  // Driver driver_6
  assign driver_7_out = y_en[6] ? x_en : 8'bz;  // Driver driver_7
  assign driver_8_out = y_en[7] ? x_en : 8'bz;  // Driver driver_8
  // Fuse_matrix fuse_matrix_1: pin names not known; wires that end beside it: {I_1, SQ[30], Q_0_t, SQ[28], I_2, SQ[26], Q_1_t, SQ[24], I_3, SQ[22], Q_2_t, SQ[20], I_4, SQ[18], Q_3_t, SQ[16], I_5, SQ[14], Q_4_t, SQ[12], I_6, SQ[10], Q_5_t, SQ[8], I_7, SQ[6], Q_6_t, SQ[4], I_8, SQ[2], Q_7_t, SQ[0]}, F, GND, driver_1_out, fuse_matrix_1_p5
  PullDown #(.Bits(8)) pulldown_3 (.out(driver_1_out));
  // Fuse_matrix fuse_matrix_2: pin names not known; wires that end beside it: {I_1, SQ[30], Q_0_t, SQ[28], I_2, SQ[26], Q_1_t, SQ[24], I_3, SQ[22], Q_2_t, SQ[20], I_4, SQ[18], Q_3_t, SQ[16], I_5, SQ[14], Q_4_t, SQ[12], I_6, SQ[10], Q_5_t, SQ[8], I_7, SQ[6], Q_6_t, SQ[4], I_8, SQ[2], Q_7_t, SQ[0]}, F, GND, driver_2_out, fuse_matrix_2_p5
  PullDown #(.Bits(8)) pulldown_4 (.out(driver_2_out));
  // Fuse_matrix fuse_matrix_3: pin names not known; wires that end beside it: {I_1, SQ[30], Q_0_t, SQ[28], I_2, SQ[26], Q_1_t, SQ[24], I_3, SQ[22], Q_2_t, SQ[20], I_4, SQ[18], Q_3_t, SQ[16], I_5, SQ[14], Q_4_t, SQ[12], I_6, SQ[10], Q_5_t, SQ[8], I_7, SQ[6], Q_6_t, SQ[4], I_8, SQ[2], Q_7_t, SQ[0]}, F, GND, driver_3_out, fuse_matrix_3_p5
  PullDown #(.Bits(8)) pulldown_5 (.out(driver_3_out));
  // Fuse_matrix fuse_matrix_4: pin names not known; wires that end beside it: {I_1, SQ[30], Q_0_t, SQ[28], I_2, SQ[26], Q_1_t, SQ[24], I_3, SQ[22], Q_2_t, SQ[20], I_4, SQ[18], Q_3_t, SQ[16], I_5, SQ[14], Q_4_t, SQ[12], I_6, SQ[10], Q_5_t, SQ[8], I_7, SQ[6], Q_6_t, SQ[4], I_8, SQ[2], Q_7_t, SQ[0]}, F, GND, driver_4_out, fuse_matrix_4_p5
  PullDown #(.Bits(8)) pulldown_6 (.out(driver_4_out));
  // Fuse_matrix fuse_matrix_5: pin names not known; wires that end beside it: {I_1, SQ[30], Q_0_t, SQ[28], I_2, SQ[26], Q_1_t, SQ[24], I_3, SQ[22], Q_2_t, SQ[20], I_4, SQ[18], Q_3_t, SQ[16], I_5, SQ[14], Q_4_t, SQ[12], I_6, SQ[10], Q_5_t, SQ[8], I_7, SQ[6], Q_6_t, SQ[4], I_8, SQ[2], Q_7_t, SQ[0]}, F, GND, driver_5_out, fuse_matrix_5_p5
  PullDown #(.Bits(8)) pulldown_7 (.out(driver_5_out));
  // Fuse_matrix fuse_matrix_6: pin names not known; wires that end beside it: {I_1, SQ[30], Q_0_t, SQ[28], I_2, SQ[26], Q_1_t, SQ[24], I_3, SQ[22], Q_2_t, SQ[20], I_4, SQ[18], Q_3_t, SQ[16], I_5, SQ[14], Q_4_t, SQ[12], I_6, SQ[10], Q_5_t, SQ[8], I_7, SQ[6], Q_6_t, SQ[4], I_8, SQ[2], Q_7_t, SQ[0]}, F, GND, driver_6_out, fuse_matrix_6_p5
  PullDown #(.Bits(8)) pulldown_8 (.out(driver_6_out));
  // Fuse_matrix fuse_matrix_7: pin names not known; wires that end beside it: {I_1, SQ[30], Q_0_t, SQ[28], I_2, SQ[26], Q_1_t, SQ[24], I_3, SQ[22], Q_2_t, SQ[20], I_4, SQ[18], Q_3_t, SQ[16], I_5, SQ[14], Q_4_t, SQ[12], I_6, SQ[10], Q_5_t, SQ[8], I_7, SQ[6], Q_6_t, SQ[4], I_8, SQ[2], Q_7_t, SQ[0]}, F, GND, driver_7_out, fuse_matrix_7_p5
  PullDown #(.Bits(8)) pulldown_9 (.out(driver_7_out));
  // Fuse_matrix fuse_matrix_8: pin names not known; wires that end beside it: {I_1, SQ[30], Q_0_t, SQ[28], I_2, SQ[26], Q_1_t, SQ[24], I_3, SQ[22], Q_2_t, SQ[20], I_4, SQ[18], Q_3_t, SQ[16], I_5, SQ[14], Q_4_t, SQ[12], I_6, SQ[10], Q_5_t, SQ[8], I_7, SQ[6], Q_6_t, SQ[4], I_8, SQ[2], Q_7_t, SQ[0]}, F, GND, driver_8_out, fuse_matrix_8_p5
  PullDown #(.Bits(8)) pulldown_10 (.out(driver_8_out));
  not not_1 (M_0[3], M_0[1]);
  // Probe on fuse_matrix_1_p5
  // Probe on fuse_matrix_2_p5
  // Probe on fuse_matrix_3_p5
  // Probe on fuse_matrix_4_p5
  // Probe on fuse_matrix_5_p5
  // Probe on fuse_matrix_6_p5
  // Probe on fuse_matrix_7_p5
  // Probe on fuse_matrix_8_p5
  // OLMC olmc_1: pin names not known; wires that end beside it: fuse_matrix_1_p5, I_9_t, I_0_Clk, I_0_Clk, nOE, M_0, olmc_1_p7, olmc_1_p8, Q_0_t, olmc_1_p7
  // OLMC olmc_2: pin names not known; wires that end beside it: fuse_matrix_2_p5, I_10_t, I_9_t, I_0_Clk, nOE, {M_1[3:2], M_0[2], M_1[0]}, olmc_2_p7, olmc_2_p8, Q_1_t, olmc_2_p7
  // OLMC olmc_3: pin names not known; wires that end beside it: fuse_matrix_3_p5, I_11_t, I_10_t, I_0_Clk, nOE, {M_1[3], M_2[2], M_1[2], M_2[0]}, olmc_3_p7, olmc_3_p8, Q_2_t, olmc_3_p7
  // OLMC olmc_4: pin names not known; wires that end beside it: fuse_matrix_4_p5, I_12_t, I_11_t, I_0_Clk, nOE, {M_1[3], M_3[2], M_2[2], M_3[0]}, olmc_4_p7, olmc_4_p8, Q_3_t, olmc_4_p7
  // OLMC olmc_5: pin names not known; wires that end beside it: fuse_matrix_5_p5, I_13_t, I_14_t, I_0_Clk, nOE, {M_1[3], M_4}, olmc_5_p7, olmc_5_p8, Q_4_t, olmc_5_p7
  // OLMC olmc_6: pin names not known; wires that end beside it: fuse_matrix_6_p5, I_14_t, I_15_t, I_0_Clk, nOE, {M_1[3], M_4[1], M_5}, olmc_6_p7, olmc_6_p8, Q_5_t, olmc_6_p7
  // OLMC olmc_7: pin names not known; wires that end beside it: fuse_matrix_7_p5, I_15_t, I_16_t, I_0_Clk, nOE, {M_1[3], M_5[1], M_6}, olmc_7_p7, olmc_7_p8, Q_6_t, olmc_7_p7
  // OLMC olmc_8: pin names not known; wires that end beside it: fuse_matrix_8_p5, I_16_t, I_17_nOE, I_0_Clk, nOE, {M_0[3], M_6[1], M_0[1], M_7[0]}, olmc_8_p7, olmc_8_p8, Q_7_t, olmc_8_p7
  // PinControl pincontrol_1: pin names not known; wires that end beside it: olmc_1_p8, I_9_t, I_9
  // PinControl pincontrol_2: pin names not known; wires that end beside it: olmc_2_p8, I_10_t, I_10
  // PinControl pincontrol_3: pin names not known; wires that end beside it: olmc_3_p8, I_11_t, I_11
  // PinControl pincontrol_4: pin names not known; wires that end beside it: olmc_4_p8, I_12_t, I_12
  // PinControl pincontrol_5: pin names not known; wires that end beside it: olmc_5_p8, I_13_t, I_13
  // PinControl pincontrol_6: pin names not known; wires that end beside it: olmc_6_p8, I_14_t, I_14
  // PinControl pincontrol_7: pin names not known; wires that end beside it: olmc_7_p8, I_15_t, I_15
  // PinControl pincontrol_8: pin names not known; wires that end beside it: olmc_8_p8, I_16_t, I_16
  PullDown pulldown_11 (.out(I_9));
  PullDown pulldown_12 (.out(I_10));
  PullDown pulldown_13 (.out(I_11));
  PullDown pulldown_14 (.out(I_12));
  PullDown pulldown_15 (.out(I_13));
  PullDown pulldown_16 (.out(I_14));
  PullDown pulldown_17 (.out(I_15));
  PullDown pulldown_18 (.out(I_16));
  not not_2 (nOE, I_17_nOE);
  not not_3 (SQ[0], Q_7_t);
  not not_4 (SQ[2], I_8);
  not not_5 (SQ[4], Q_6_t);
  not not_6 (SQ[6], I_7);
  not not_7 (SQ[8], Q_5_t);
  not not_8 (SQ[10], I_6);
  not not_9 (SQ[12], Q_4_t);
  not not_10 (SQ[14], I_5);
  not not_11 (SQ[16], Q_3_t);
  not not_12 (SQ[18], I_4);
  not not_13 (SQ[20], Q_2_t);
  not not_14 (SQ[22], I_3);
  not not_15 (SQ[24], Q_1_t);
  not not_16 (SQ[26], I_2);
  not not_17 (SQ[28], Q_0_t);
  not not_18 (SQ[30], I_1);

  assign Q_0 = I_9;
  assign Q_1 = I_10;
  assign Q_2 = I_11;
  assign Q_3 = I_12;
  assign Q_4 = I_13;
  assign Q_5 = I_14;
  assign Q_6 = I_15;
  assign Q_7 = I_16;

  // Other names for the same wires on the sheet: M_2 (some bits) = M_1[3:2]; M_3 (some bits) = {M_1[3], M_2[2]};
  //   M_4[3] = M_1[3]; M_5[3:2] = {M_1[3], M_4[1]}; M_6[3:2] = {M_1[3], M_5[1]}; M_7[3:1] = {M_0[3], M_6[1], M_0[1]};
  //   M_1[1] = M_0[2]; C = GND; Clk = I_0_Clk; I_0 = I_0_Clk;
  //   SQ (some bits) = {I_1, Q_0_t, I_2, Q_1_t, I_3, Q_2_t, I_4, Q_3_t, I_5, Q_4_t, I_6, Q_5_t, I_7, Q_6_t, I_8, Q_7_t};
  //   I_17 = I_17_nOE

  // Notes on the sheet:
  //   GND: Hz: 50
  //   contents of Fuses (hex, n*v repeats v):
  //   7fff7bff,efffbbff,6*ffffffff,f7ff7bff,deffbbff,edffbbff,5*ffffffff
  //   ,ff7f7bff,fedfbbff,efdfbbff,ddefbbff,4*ffffffff,fff77bff,ffedbbff
  //   ,fefdbbff,effdbbff,dddebbff,35*ffffffff,f0007fff
endmodule
