// Digital circuit GAL16V8_Test.dig as structural Verilog
module GAL16V8_Test (
  input  D_0,
  input  Set,
  input  Clr,
  input  clk,
  input  nOE,
  input  D_1,
  input  D_2,
  input  D_3
);

  wire Clk_out, gal16v8_1_q_0, gal16v8_1_q_1, gal16v8_1_q_2, gal16v8_1_q_3, gal16v8_1_q_4, gal16v8_1_q_5,
       gal16v8_1_q_6, gal16v8_1_q_7, gal16v8_1_vcc;

  Button u_Clk (.out(Clk_out));
  GAL16V8 gal16v8_1 (
    .Q_7(gal16v8_1_q_7), .I_0_Clk(Clk_out), .I_1(D_0), .Q_6(gal16v8_1_q_6), .Q_5(gal16v8_1_q_5),
    .Q_4(gal16v8_1_q_4), .Q_3(gal16v8_1_q_3), .Q_2(gal16v8_1_q_2), .Q_1(gal16v8_1_q_1), .Q_0(gal16v8_1_q_0),
    .I_2(D_1), .I_3(D_2), .I_4(D_3), .I_5(Set), .I_6(Clr), .I_7(1'b0), .I_8(1'b0), .GND(clk), .I_17_nOE(nOE),
    .VCC(gal16v8_1_vcc), .I_9(gal16v8_1_q_0), .I_10(gal16v8_1_q_1), .I_11(gal16v8_1_q_2),
    .I_12(gal16v8_1_q_3), .I_13(gal16v8_1_q_4), .I_14(gal16v8_1_q_5), .I_15(gal16v8_1_q_6),
    .I_16(gal16v8_1_q_7));
  LED Ready (.in(gal16v8_1_vcc));
  LED Q_0 (.in(gal16v8_1_q_0));
  LED Q_1 (.in(gal16v8_1_q_1));
  LED Q_2 (.in(gal16v8_1_q_2));
  LED Q_3 (.in(gal16v8_1_q_3));

  // Notes on the sheet:
  //   clk: Hz: 50
endmodule
